# Fritzing sketch circuit.00.schematics (saved by Fritzing 0.9.3b)
breadboards: 1

parts:
  pushbutton = Momentary Switch [package=ksa_sealed_tac_switch]
  resistor = Resistor [tolerance=±5% resistance=220 package="2010 [SMD]"]
  microcontroller = Arduino Uno (Rev3)

nets:
  N1: pushbutton.1, resistor.Pin_0, microcontroller.A0
  N2: pushbutton.3, microcontroller.GND
  N3: resistor.Pin_1, microcontroller.5V
