# Fritzing sketch circuit.01.schematics (saved by Fritzing 0.9.3b)
breadboards: 1

parts:
  Microcontroller = Arduino Uno (Rev3)
  Potentiometer = POT [package=pot_mammoth]

nets:
  N1: Microcontroller.A0, Potentiometer.S
  N2: Microcontroller.5V, Potentiometer.E
  N3: Microcontroller.GND, Potentiometer.A
