# Fritzing sketch circuit.02.schematics (saved by Fritzing 0.9.3b)
breadboards: 1

parts:
  Microcontroller = Arduino Uno (Rev3)
  Photoresistor = PHOTOCELL [package=photocell-kit]
  R = Resistor [tolerance=±5% resistance=220 package=THT]

nets (from the schematic view):
  N1: Microcontroller.A0, Photoresistor.P$1, R.Pin_0
  N2: Microcontroller.GND, Photoresistor.P$2
  N3: Microcontroller.5V, R.Pin_1
