# Fritzing sketch circuit.03.schematics (saved by Fritzing 0.9.3b)
breadboards: 1

parts:
  Microcontroller = Arduino Uno (Rev3)
  LED = LED - 5mm [color="Red (633nm)" package="5 mm [THT]"]
  Photoresistor = PHOTOCELL [package=photocell-kit]
  R = Resistor [tolerance=±5% resistance=220 package=THT]

nets:
  N1: Microcontroller.A0, Photoresistor.P$1, R.Pin_0
  N2: Microcontroller.GND, LED.cathode, Photoresistor.P$2
  N3: Microcontroller.D2, LED.anode
  N4: Microcontroller.5V, R.Pin_1
