# Fritzing sketch circuit.04.schematics (saved by Fritzing 0.9.3b)
breadboards: 1

parts:
  Microcontroller = Arduino Uno (Rev3)
  LED = LED - 5mm [color="Red (633nm)" package="5 mm [THT]"]
  LED_2 = LED - 5mm [color="Green (560nm)" package="5 mm [THT]"]
  Photoresisor = PHOTOCELL [package=photocell-kit]
  R = Resistor [tolerance=±5% resistance=220 package=THT]

nets:
  N1: Microcontroller.A0, Photoresisor.P$1, R.Pin_0
  N2: Microcontroller.GND, LED.cathode, LED_2.cathode, Photoresisor.P$2
  N3: Microcontroller.D2, LED.anode
  N4: Microcontroller.D4, LED_2.anode
  N5: Microcontroller.5V, R.Pin_1
