# Fritzing sketch circuit.05.schematics (saved by Fritzing 0.9.3b)
breadboards: 1

parts:
  LED = LED - 5mm [color="Red (633nm)" package="5 mm [THT]"]
  Microcontroller = Arduino Uno (Rev3)
  LED_2 = LED - 5mm [color="Green (560nm)" package="5 mm [THT]"]
  LED_3 = LED - 5mm [color="Yellow (574nm)" package="5 mm [THT]"]
  Photoresistor = PHOTOCELL [package=photocell-kit]
  R1 = Resistor [tolerance=±5% resistance=220 package=THT]

nets:
  N1: LED.cathode, Microcontroller.GND, LED_2.cathode, LED_3.cathode, Photoresistor.P$2
  N2: LED.anode, Microcontroller.D2
  N3: Microcontroller.A0, Photoresistor.P$1, R1.Pin_0
  N4: Microcontroller.D3_PWM, LED_3.anode
  N5: Microcontroller.D4, LED_2.anode
  N6: Microcontroller.5V, R1.Pin_1
